# Fritzing sketch server_sketch (saved by Fritzing 0.9.3b)
breadboards: 1

parts:
  Bauteil2 = Adafruit Feather HUZZAH ESP8266 [part_number="Adafruit #2821"]
  R1 = Photocell (LDR) [package=THT]
  R2 = Resistor [tolerance=±5% resistance=220 package=THT]

nets:
  N1: Bauteil2.ADC, R1.pin_1, R2.Pin_0
  N2: Bauteil2.GND, R2.Pin_1
  N3: Bauteil2.3.3V, R1.pin_0

custom parts:
  Adafruit Feather HUZZAH ESP8266: his is the Adafruit Feather HUZZAH ESP8266 - our take on an 'all-in-one' ESP8266 WiFi development board with built in USB and battery charging. Its an ESP8266 WiFi module with all the extras you need, ready to rock! We have other boards in the Feather family, check'em out here. At the Feather HUZZAH's heart is an ESP8266 WiFi microcontroller clocked at 80 MHz and at 3.3V logic. This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
